# Fritzing sketch Reed Switch  (saved by Fritzing 0.9.10b)

parts:
  S63 = Reed switch [package=THT]
  S64 = Reed switch [package=THT]
  S62 = Reed switch [package=THT]
  S12 = Reed switch [package=THT]
  S5 = Reed switch [package=THT]
  S6 = Reed switch [package=THT]
  S4 = Reed switch [package=THT]
  S59 = Reed switch [package=THT]
  S48 = Reed switch [package=THT]
  S7 = Reed switch [package=THT]
  S54 = Reed switch [package=THT]
  S26 = Reed switch [package=THT]
  S20 = Reed switch [package=THT]
  S60 = Reed switch [package=THT]
  S11 = Reed switch [package=THT]
  S42 = Reed switch [package=THT]
  S25 = Reed switch [package=THT]
  S23 = Reed switch [package=THT]
  S58 = Reed switch [package=THT]
  S22 = Reed switch [package=THT]
  S53 = Reed switch [package=THT]
  S55 = Reed switch [package=THT]
  S30 = Reed switch [package=THT]
  S13 = Reed switch [package=THT]
  S46 = Reed switch [package=THT]
  S19 = Reed switch [package=THT]
  S39 = Reed switch [package=THT]
  S52 = Reed switch [package=THT]
  S1 = Reed switch [package=THT]
  S40 = Reed switch [package=THT]
  S47 = Reed switch [package=THT]
  S45 = Reed switch [package=THT]
  S37 = Reed switch [package=THT]
  S38 = Reed switch [package=THT]
  S29 = Reed switch [package=THT]
  S50 = Reed switch [package=THT]
  S27 = Reed switch [package=THT]
  S57 = Reed switch [package=THT]
  S2 = Reed switch [package=THT]
  S56 = Reed switch [package=THT]
  S32 = Reed switch [package=THT]
  S51 = Reed switch [package=THT]
  S16 = Reed switch [package=THT]
  S43 = Reed switch [package=THT]
  S44 = Reed switch [package=THT]
  S28 = Reed switch [package=THT]
  S36 = Reed switch [package=THT]
  S49 = Reed switch [package=THT]
  S41 = Reed switch [package=THT]
  S3 = Reed switch [package=THT]
  S31 = Reed switch [package=THT]
  S15 = Reed switch [package=THT]
  S24 = Reed switch [package=THT]
  S10 = Reed switch [package=THT]
  S35 = Reed switch [package=THT]
  S17 = Reed switch [package=THT]
  S21 = Reed switch [package=THT]
  S18 = Reed switch [package=THT]
  S9 = Reed switch [package=THT]
  S34 = Reed switch [package=THT]
  S8 = Reed switch [package=THT]
  S14 = Reed switch [package=THT]
  S33 = Reed switch [package=THT]
  S61 = Reed switch [package=THT]
  Part1 = Arduino Mega 2560 (Rev3)

nets:
  N1: S63.pin_1, S64.pin_1, S62.pin_1, S59.pin_1, S60.pin_1, S58.pin_1, S57.pin_1, S61.pin_1, Part1.D37
  N2: S63.pin_2, S23.pin_2, S55.pin_2, S39.pin_2, S47.pin_2, S2.pin_2, S31.pin_2, S15.pin_2, Part1.D28
  N3: S64.pin_2, S48.pin_2, S40.pin_2, S56.pin_2, S32.pin_2, S16.pin_2, S3.pin_2, S24.pin_2, Part1.D27
  N4: S62.pin_2, S4.pin_2, S54.pin_2, S22.pin_2, S30.pin_2, S46.pin_2, S38.pin_2, S14.pin_2, Part1.D26
  N5: S12.pin_1, S11.pin_1, S13.pin_1, S16.pin_1, S15.pin_1, S10.pin_1, S9.pin_1, S14.pin_1, Part1.D31
  N6: S12.pin_2, S7.pin_2, S20.pin_2, S60.pin_2, S53.pin_2, S13.pin_2, S52.pin_2, S45.pin_2, S37.pin_2, S29.pin_2, S44.pin_2, S28.pin_2, S36.pin_2, S21.pin_2, S8.pin_2, S61.pin_2, Part1.D22, Part1.D23
  N7: S5.pin_1, S6.pin_1, S4.pin_1, S7.pin_1, S1.pin_1, S2.pin_1, S3.pin_1, S8.pin_1, Part1.D30
  N8: S5.pin_2, S26.pin_2, S42.pin_2, S58.pin_2, S50.pin_2, S10.pin_2, S18.pin_2, S34.pin_2, Part1.D25
  N9: S6.pin_2, S59.pin_2, S11.pin_2, S19.pin_2, S27.pin_2, S51.pin_2, S43.pin_2, S35.pin_2, Part1.D24
  N10: S48.pin_1, S42.pin_1, S46.pin_1, S47.pin_1, S45.pin_1, S43.pin_1, S44.pin_1, S41.pin_1, Part1.D35
  N11: S54.pin_1, S53.pin_1, S55.pin_1, S52.pin_1, S50.pin_1, S56.pin_1, S51.pin_1, S49.pin_1, Part1.D36
  N12: S26.pin_1, S25.pin_1, S30.pin_1, S29.pin_1, S27.pin_1, S32.pin_1, S28.pin_1, S31.pin_1, Part1.D33
  N13: S20.pin_1, S23.pin_1, S22.pin_1, S19.pin_1, S24.pin_1, S17.pin_1, S21.pin_1, S18.pin_1, Part1.D32
  GND: S25.pin_2, S1.pin_2, S57.pin_2, S49.pin_2, S41.pin_2, S17.pin_2, S9.pin_2, S33.pin_2, Part1.D29
  N14: S39.pin_1, S40.pin_1, S37.pin_1, S38.pin_1, S36.pin_1, S35.pin_1, S34.pin_1, S33.pin_1, Part1.D34
