# Fritzing sketch fritzing-diagram_lab1 (saved by Fritzing 0.9.3b)
breadboards: 1

parts:
  Part1 = Arduino Mega 2560 (Rev3)
  R1 = Resistor [tolerance=±5% resistance=100 package=THT]
  R2 = Resistor [tolerance=±5% resistance=100 package=THT]
  R3 = Resistor [tolerance=±5% resistance=100 package=THT]
  R4 = Resistor [tolerance=±5% resistance=100 package=THT]
  R5 = Resistor [tolerance=±5% resistance=100 package=THT]
  R6 = Resistor [tolerance=±5% resistance=100 package=THT]
  LED1 = LED - 5mm [color="Red (633nm)" package="5 mm [THT]"]
  LED2 = LED - 5mm [color="Yellow (595nm)" package="5 mm [THT]"]
  LED3 = LED - 5mm [color="Green (565nm)" package="5 mm [THT]"]
  LED4 = LED - 5mm [color="Red (633nm)" package="5 mm [THT]"]
  LED5 = LED - 5mm [color="Yellow (595nm)" package="5 mm [THT]"]
  LED6 = LED - 5mm [color="Green (565nm)" package="5 mm [THT]"]
  SW1 = DIP SWITCH [package=dipswitch-02]
  R7 = Resistor [tolerance=±5% resistance=100 package=THT]
  R8 = Resistor [tolerance=±5% resistance=100 package=THT]

nets:
  N1: Part1.GND, R1.Pin_1, R2.Pin_1, R3.Pin_1, R4.Pin_1, R5.Pin_1, R6.Pin_1, R7.Pin_1, R8.Pin_1
  N2: Part1.D13_PWM, LED1.anode
  N3: Part1.D12_PWM, LED2.anode
  N4: Part1.D11_PWM, LED3.anode
  N5: Part1.D9_PWM, SW1.1
  N6: Part1.D8_PWM, SW1.2
  N7: Part1.D3_PWM, LED6.anode
  N8: Part1.D4_PWM, LED5.anode
  N9: Part1.D5_PWM, LED4.anode
  N10: R1.Pin_0, LED1.cathode
  N11: R2.Pin_0, LED2.cathode
  N12: R3.Pin_0, LED3.cathode
  N13: R4.Pin_0, LED4.cathode
  N14: R5.Pin_0, LED5.cathode
  N15: R6.Pin_0, LED6.cathode
  N16: SW1.3, R8.Pin_0
  N17: SW1.4, R7.Pin_0

// code stored in the sketch: fritzing-diagram_lab1.fzz.ino
/*-------------------------------------------------------------
Name: Josiah Tsang
Student #: 10032https://create.arduino.cc/821
Date: Jan 25, 2020
Case Study Lab 1: Traffic Light Controller
*/

//variables
int signalMain[] = {3, 4, 5}; // main street - green/yellow/red 
int signalCross[] = {11, 12, 13}; // cross street - green/yellow/red 
int delayLight[3]; // array to store time delay for each light
int setting = 0; 
const int switch1 = 8, switch2 = 9;
const int yelBlink = 500;
                 
//timing
int timing[4][3] = {{1000, 1000, 2000}, // green/yellow/red
                   {5000, 1000, 6000}, 
                   {6000, 2000, 8000},
                   {15000, 5000, 20000}};
                  
void setup(){ // setup function runs once board is reset or powered
  
  for (int i = 0; i < 3; i++){ // initalize each trafic light and set default state to off (NOTE: OPEN ON SWITCH IS HIGH)
    pinMode(signalMain[i], OUTPUT);
    pinMode(signalCross[i], OUTPUT);
    digitalWrite(signalMain[i], LOW);
    digitalWrite(signalCross[i], LOW);
  }
  //switches
    pinMode(switch1, INPUT_PULLUP); // initalize DIP switches
    pinMode(switch2, INPUT_PULLUP);
    
}

void loop(){ // loop function repeats forever
  
  if (digitalRead(switch1) == LOW && digitalRead(switch2) == LOW)
    setting = 0;
  else if (digitalRead(switch1) == LOW && digitalRead(switch2) == HIGH)
    setting = 1;
  else if (digitalRead(switch1) == HIGH && digitalRead(switch2) == LOW)
    setting = 2;
  else if (digitalRead(switch1) == HIGH && digitalRead(switch2) == HIGH)
    setting = 3;
  else 
    setting = 3; // default if no switches 
  
  for (int i = 0; i < 3; i++)
      delayLight[i] = timing[setting][i];
      
  changeLights();
}

void changeLights(){
  // state 0  
  digitalWrite(signalMain[0], HIGH); // main green on, cross red off
  digitalWrite(signalMain[2], LOW);
  digitalWrite(signalCross[2], HIGH);
  delay(delayLight[0]);
  
  // state 1
  digitalWrite(signalMain[0], LOW); // main green off, main yellow blink
  blinkYellow(signalMain[1], delayLight[1]);
  
  // state 2
  digitalWrite(signalMain[1], LOW); // main yellow off, main red on, cross green on, cross red off
  digitalWrite(signalMain[2], HIGH);
  digitalWrite(signalCross[0], HIGH);
  digitalWrite(signalCross[2], LOW);
  delay(delayLight[2]);
  
  // state 3
  digitalWrite(signalCross[0], LOW); // cross green off, cross yellow blink
  blinkYellow(signalCross[1], delayLight[1]);
}

void blinkYellow(int yellow, int yelDelay){
  for (int i = 0; i < yelDelay/yelBlink; i++){
    digitalWrite(yellow, HIGH);   
    delay(yelBlink);                       
    digitalWrite(yellow, LOW);    
    delay(yelBlink);   
  }
}
