# Fritzing sketch leetChess_elecCircuit (saved by Fritzing 0.9.3b)

parts:
  IC1 = SELECTOR_MULTIPLEXER [package=dil16]
  S1 = SWITCH-MOMENTARY-2 [package=reed_switch_pth]
  Part1 = Adafruit TCA9548A
  Part2 = HT16K33 Breakout 16x8 LED Matrix Driver [part_number=1427]
  S2 = SWITCH-MOMENTARY-2 [package=reed_switch_pth]  # not connected
  IC2 = SELECTOR_MULTIPLEXER [package=dil16]
  S3 = SWITCH-MOMENTARY-2 [package=reed_switch_pth]  # not connected
  S4 = SWITCH-MOMENTARY-2 [package=reed_switch_pth]  # not connected
  S5 = SWITCH-MOMENTARY-2 [package=reed_switch_pth]  # not connected
  S6 = SWITCH-MOMENTARY-2 [package=reed_switch_pth]  # not connected
  S7 = SWITCH-MOMENTARY-2 [package=reed_switch_pth]  # not connected
  S8 = SWITCH-MOMENTARY-2 [package=reed_switch_pth]  # not connected
  S9 = SWITCH-MOMENTARY-2 [package=reed_switch_pth]  # not connected
  S10 = SWITCH-MOMENTARY-2 [package=reed_switch_pth]  # not connected
  S11 = SWITCH-MOMENTARY-2 [package=reed_switch_pth]  # not connected
  S12 = SWITCH-MOMENTARY-2 [package=reed_switch_pth]  # not connected
  S13 = SWITCH-MOMENTARY-2 [package=reed_switch_pth]  # not connected
  S14 = SWITCH-MOMENTARY-2 [package=reed_switch_pth]  # not connected
  S15 = SWITCH-MOMENTARY-2 [package=reed_switch_pth]  # not connected
  S16 = SWITCH-MOMENTARY-2 [package=reed_switch_pth]  # not connected
  IC3 = SELECTOR_MULTIPLEXER [package=dil16]
  IC4 = SELECTOR_MULTIPLEXER [package=dil16]
  S17 = SWITCH-MOMENTARY-2 [package=reed_switch_pth]  # not connected
  S18 = SWITCH-MOMENTARY-2 [package=reed_switch_pth]  # not connected
  S19 = SWITCH-MOMENTARY-2 [package=reed_switch_pth]
  S20 = SWITCH-MOMENTARY-2 [package=reed_switch_pth]  # not connected
  S21 = SWITCH-MOMENTARY-2 [package=reed_switch_pth]  # not connected
  S22 = SWITCH-MOMENTARY-2 [package=reed_switch_pth]  # not connected
  S23 = SWITCH-MOMENTARY-2 [package=reed_switch_pth]  # not connected
  S24 = SWITCH-MOMENTARY-2 [package=reed_switch_pth]  # not connected
  S25 = SWITCH-MOMENTARY-2 [package=reed_switch_pth]  # not connected
  S26 = SWITCH-MOMENTARY-2 [package=reed_switch_pth]  # not connected
  S27 = SWITCH-MOMENTARY-2 [package=reed_switch_pth]  # not connected
  S28 = SWITCH-MOMENTARY-2 [package=reed_switch_pth]  # not connected
  S29 = SWITCH-MOMENTARY-2 [package=reed_switch_pth]  # not connected
  S30 = SWITCH-MOMENTARY-2 [package=reed_switch_pth]  # not connected
  S31 = SWITCH-MOMENTARY-2 [package=reed_switch_pth]  # not connected
  S32 = SWITCH-MOMENTARY-2 [package=reed_switch_pth]  # not connected
  IC5 = SELECTOR_MULTIPLEXER [package=dil16]
  IC6 = SELECTOR_MULTIPLEXER [package=dil16]
  S33 = SWITCH-MOMENTARY-2 [package=reed_switch_pth]  # not connected
  S34 = SWITCH-MOMENTARY-2 [package=reed_switch_pth]  # not connected
  S35 = SWITCH-MOMENTARY-2 [package=reed_switch_pth]  # not connected
  S36 = SWITCH-MOMENTARY-2 [package=reed_switch_pth]  # not connected
  S37 = SWITCH-MOMENTARY-2 [package=reed_switch_pth]  # not connected
  S38 = SWITCH-MOMENTARY-2 [package=reed_switch_pth]  # not connected
  S39 = SWITCH-MOMENTARY-2 [package=reed_switch_pth]  # not connected
  S40 = SWITCH-MOMENTARY-2 [package=reed_switch_pth]  # not connected
  S41 = SWITCH-MOMENTARY-2 [package=reed_switch_pth]  # not connected
  S42 = SWITCH-MOMENTARY-2 [package=reed_switch_pth]  # not connected
  S43 = SWITCH-MOMENTARY-2 [package=reed_switch_pth]  # not connected
  S44 = SWITCH-MOMENTARY-2 [package=reed_switch_pth]  # not connected
  S45 = SWITCH-MOMENTARY-2 [package=reed_switch_pth]  # not connected
  S46 = SWITCH-MOMENTARY-2 [package=reed_switch_pth]
  S47 = SWITCH-MOMENTARY-2 [package=reed_switch_pth]  # not connected
  S48 = SWITCH-MOMENTARY-2 [package=reed_switch_pth]  # not connected
  IC7 = SELECTOR_MULTIPLEXER [package=dil16]
  IC8 = SELECTOR_MULTIPLEXER [package=dil16]
  S49 = SWITCH-MOMENTARY-2 [package=reed_switch_pth]  # not connected
  S50 = SWITCH-MOMENTARY-2 [package=reed_switch_pth]  # not connected
  S51 = SWITCH-MOMENTARY-2 [package=reed_switch_pth]  # not connected
  S52 = SWITCH-MOMENTARY-2 [package=reed_switch_pth]  # not connected
  S53 = SWITCH-MOMENTARY-2 [package=reed_switch_pth]  # not connected
  S54 = SWITCH-MOMENTARY-2 [package=reed_switch_pth]  # not connected
  S55 = SWITCH-MOMENTARY-2 [package=reed_switch_pth]  # not connected
  S56 = SWITCH-MOMENTARY-2 [package=reed_switch_pth]  # not connected
  S57 = SWITCH-MOMENTARY-2 [package=reed_switch_pth]  # not connected
  S58 = SWITCH-MOMENTARY-2 [package=reed_switch_pth]  # not connected
  S59 = SWITCH-MOMENTARY-2 [package=reed_switch_pth]  # not connected
  S60 = SWITCH-MOMENTARY-2 [package=reed_switch_pth]  # not connected
  S61 = SWITCH-MOMENTARY-2 [package=reed_switch_pth]  # not connected
  S62 = SWITCH-MOMENTARY-2 [package=reed_switch_pth]
  S63 = SWITCH-MOMENTARY-2 [package=reed_switch_pth]  # not connected
  S64 = SWITCH-MOMENTARY-2 [package=reed_switch_pth]  # not connected
  Part3 = LED Matrix - Serial Interface - Red/Green/Blue
  Raspberry_Pi_2 = Raspberry Pi 4 [part_number=RPI-4-b]  # not connected
  Part4 = Arduino Uno (Rev3)

nets:
  VCC: IC1.P_VCC, Part1.VCC, Part2.VDD, IC3.P_VCC, IC5.P_VCC, IC8.P_VCC, Part4.5V
  N1: S1.1, IC2.A_!A!_B
  N2: S1.2, IC2.A_1A
  N3: Part1.2SDA, IC2.P_VCC
  N4: Part1.2SCL, IC2.A_G
  N5: Part1.3SDA, IC4.P_VCC
  N6: Part1.3SCL, IC4.A_G
  N7: Part1.4SDA, IC6.P_VCC
  N8: Part1.4SCL, IC6.A_G
  N9: Part1.5SDA, IC7.P_VCC
  N10: Part1.5SCL, IC7.A_G
  GND: Part1.GND, Part3.GND, Part4.GND
  N11: Part1.INPUTSDA, Part4.A5/SCL
  N12: Part1.INPUTSCL, Part4.A4/SDA
  N13: Part1.1SDA, Part2.SDA
  N14: Part1.1SCL, Part2.SCL
  N15: Part2.GND, IC2.A_3Y, IC4.A_3Y, IC6.A_3Y, IC7.A_3Y
  N16: IC4.A_!A!_B, S19.1
  N17: IC4.A_1A, S19.2
  N18: IC6.A_!A!_B, S46.1
  N19: IC6.A_1A, S46.2
  N20: IC7.A_!A!_B, S62.1
  N21: IC7.A_1A, S62.2
  VCC_2: Part3.VCC, Part4.3V3

notes:
  8 x 8 LED MATRIX MADE WITH ADDRESSABLE NEOPIXEL LED STRIPS
  8 x 8 REED SWITCHES (SENSORS)
  RASBERRY PI
  PORT EXPANDERS
  LED MATRIX DRIVER
  I2C MULTIPLEXER
  ARDUINO UNO

custom parts:
  Adafruit TCA9548A: You just found the perfect I2C sensor, and you want to wire up two or three or more of them to your Arduino when you realize "Uh oh, this chip has a fixed I2C address, and from what I know about I2C, you cannot have two devices with the same address on the same SDA/SCL pins!" Are you out of luck? You would be, if you didn't have this ultra-cool TCA9548A 1-to-8 I2C multiplexer! Finally, a way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
  HT16K33 Breakout 16x8 LED Matrix Driver: This is the magic sauce in our 7-segment and matrix backpacks, now available in breadboard-friendly breakout board format. The HT16K33 is a neat little chip that has the ability to drive a multiplexed 16x8 matrix (that's 128 individual LEDs). The communication protocol is I2C so it uses only 2 pins, and you can have up to 8 selectable I2C addresses so thats a total of 8 matrices, each one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
  Raspberry Pi 4: The RPi4, a faster version of the awesome Raspberry Pi 2 B ARM Board with 40 pin gpio. Ready for special Raspberry Pi B+ and RPi2 Hat (Hardware attached (on) top)
