# Fritzing sketch reedSwitches (saved by Fritzing 0.9.3b)
breadboards: 1

parts:
  S1 = SWITCH-MOMENTARY-2 [package=reed_switch_plastic]
  S2 = SWITCH-MOMENTARY-2 [package=reed_switch_plastic]
  S3 = SWITCH-MOMENTARY-2 [package=reed_switch_pth]
  S4 = SWITCH-MOMENTARY-2 [package=reed_switch_pth]
  Part1 = Arduino Uno (Rev3) - ICSP
  S5 = SWITCH-MOMENTARY-2 [package=reed_switch_plastic]
  S6 = SWITCH-MOMENTARY-2 [package=reed_switch_plastic]

nets:
  N1: S1.1, S2.1, S3.1, S4.1, Part1.D8, Part1.D9_PWM, Part1.D10_PWM/SS, Part1.GND, S5.1, S6.1
  N2: S1.2, S2.2, Part1.D2, S6.2
  N3: S3.2, S4.2, Part1.D3_PWM, S5.2

notes:
  COLUMNS - X
  (PINS 8 - 10)
  ROWS - Y
  (PINS 2 - 3)
  0
  1
  2

// code stored in the sketch: reedSwitches_nxn.ino
/*
  Test of 6 x 6 Reed Switches
  using input pins 2-7 for columns
  and input pins 8-13 for rows
*/

#include <Adafruit_NeoPixel.h>
# define BOARD_SIZE 2       // number of columns and rows in the board
#define N_LEDS 8 * 8        // number of individual LEDs in one neopixel strip
#define BOARD_PIN 12        // pin for the neopixel strip
int columnPins[] = {8, 9, 10};  // pins for columns
int rowPins[] = {2, 3};     // pins for rows

void setup() {
  // initialize serial communication
  Serial.begin(9600);

  // initialize columns to output
  for (int i = 0; i < sizeof(columnPins)/sizeof(int); i++)
    pinMode(columnPins[i], OUTPUT);

  // initialize rows to input
  for (int i = 0; i < sizeof(rowPins)/sizeof(int); i++)
    pinMode(rowPins[i], INPUT);

  /* 
    initialize neopixel strip here // TODO
  */
}

void loop() {
  // constantly check for changes in the grid
  checkGrid();
  delay(1000);
}

void checkGrid() {
  for (int i = 0; i < sizeof(columnPins)/sizeof(int); i++) {
    digitalWrite(columnPins[i], HIGH);
    for (int j = 0; j < sizeof(rowPins)/sizeof(int); j++) {
      if (digitalRead(rowPins[j]) == HIGH)
        setLED(i, j); // TODO: update to setLED(x, y) function
      else
        clearLED(i, j); // TODO: update to clearLED(x, y) function
    }
    digitalWrite(columnPins[i], LOW);
  }
}

void setLED(int x, int y) {
  Serial.print("LED is on at: ");
  Serial.print(x);
  Serial.print(',');
  Serial.print(y);
  Serial.println();
  // strip.setPixelColor(matrix[x][y], c);
  // strip.show();
}

// turn off a single LED
void clearLED(int x, int y) {
  Serial.print("LED is off at: ");
  Serial.print(x);
  Serial.print(',');
  Serial.print(y);
  Serial.println();
  // strip.setPixelColor(matrix[x][y], strip.Color(0, 0, 0, 0));
  // strip.show();
}
